# Fritzing sketch Шаблон электросхемы проекта-ivan (saved by Fritzing 0.9.3b)
breadboards: 1

parts:
  VCC1 = Battery
  S1 = Toggle Switch [package=THT]
  Disp1 = LBT2088AH [part_number=LBT2088AH]
  S2 = Pushbutton [package="[THT]"]
  S3 = Pushbutton [package="[THT]"]
  LED1 = LED - 5mm [color="Green (570nm)" package="5 mm [THT]"]
  R1 = Resistor [tolerance=±5% resistance=220 package=THT]
  Часть1 = Arduino Uno (Rev3)

nets:
  N1: VCC1.-, S1.L1
  N2: VCC1.+, Disp1.pin_16, Часть1.VIN
  N3: S1.L2, Disp1.pin_15, S2.Pin_1, S2.Pin_2, S3.Pin_1, S3.Pin_2, R1.Pin_1, Часть1.GND
  N4: Disp1.pin_14, Часть1.D5_PWM
  N5: S2.Pin_3, S2.Pin_4, Часть1.D2
  N6: S3.Pin_3, S3.Pin_4, Часть1.D4
  N7: LED1.cathode, Часть1.D3_PWM
  N8: LED1.anode, R1.Pin_0
